# Fritzing sketch prototype (saved by Fritzing 0.9.3b)
circuit board: 16.0141cm x 7.28229cm
breadboards: 1

parts:
  Adafruit_Bluefruit_LE_UART_Friend = Adafruit Bluefruit LE UART Friend [part_number="Adafruit #2479"]
  AD8232 = AD8232 HeartRate Monitor [part_number=SEN-12650 chip_label=IC package="DIP (Dual Inline) [THT]"]
  Arduino_Nano = Arduino Nano (Rev3.0) (ICSP)
  S1 = Pushbutton [package="[THT]"]

nets:
  N1: Adafruit_Bluefruit_LE_UART_Friend.DFU, S1.Pin_3, S1.Pin_4
  GND: Adafruit_Bluefruit_LE_UART_Friend.GND, AD8232.GND, Arduino_Nano.GND, S1.Pin_1, S1.Pin_2
  N2: Adafruit_Bluefruit_LE_UART_Friend.RTS, Arduino_Nano.D8
  VIN: Adafruit_Bluefruit_LE_UART_Friend.VIN, Arduino_Nano.5V
  N3: Adafruit_Bluefruit_LE_UART_Friend.RXI, Arduino_Nano.D9
  N4: Adafruit_Bluefruit_LE_UART_Friend.TXO, Arduino_Nano.D10
  N5: Adafruit_Bluefruit_LE_UART_Friend.CTS, Arduino_Nano.D11/MOSI
  N6: Adafruit_Bluefruit_LE_UART_Friend.MODE, Arduino_Nano.D12/MISO
  3.3V: AD8232.3.3v, Arduino_Nano.3V3
  N7: AD8232.OUTPUT, Arduino_Nano.A0
  N8: AD8232.LO-, Arduino_Nano.D3
  N9: AD8232.LO+, AD8232.SDN, Arduino_Nano.D4
  N10: AD8232.LA, AD8232.RL

custom parts:
  Adafruit Bluefruit LE UART Friend: The Bluefruit LE UART Friend makes it easy to add Bluetooth Low Energy connectivity to anything with a hardware or software serial port. We even have nice hardware flow control so you won't have to think about losing data. Connect to your Arduino or other microcontroller or even just a standard FTDI cable for debugging and testing.
  AD8232 HeartRate Monitor: A DIP stand-in part for whatever IC you want. With 10 pins on a 600mil dual inline package (DIP) footprint.
